# Fritzing sketch ESP Вариант (saved by Fritzing 0.9.5d)
breadboards: 1

parts:
  WeMos_D1_Mini1 = WeMos D1 Mini  # not connected
  DFRobot_DFPlayer_Mini1 = DFRobot DFPlayer Mini [part_number=DFR0299]
  SP1 = SPEAKER [package=pcb_mount_speaker]
  S2 = Momentary Switch [package=ksa_sealed_tac_switch]
  R1 = Resistor [tolerance=±5% resistance=10k package="1206 [SMD]"]
  L298N1 = L298N DC motor driver
  M1 = DC Motor
  VCC1 = Battery block 9V

nets:
  N1: DFRobot_DFPlayer_Mini1.SPK_1, SP1.-
  N2: DFRobot_DFPlayer_Mini1.GND-1, DFRobot_DFPlayer_Mini1.GND-2, R1.Pin_0, L298N1.GND, VCC1.-
  N3: DFRobot_DFPlayer_Mini1.SPK_2, SP1.+
  N4: S2.4, R1.Pin_1
  N5: L298N1.OUT3, M1.pin_2
  N6: L298N1.OUT4, M1.pin_1
  N7: L298N1.12V, VCC1.+
  N8: L298N1.5V, L298N1.ENB

custom parts:
  L298N DC motor driver: 2x DC motor driver with 78M05 positive voltage regulator (7..35 V) L298N: max 46 V, 2 A Set 5 V Enable jumper to enable 5 V regultor (needed for the L298N) and +5 V output at screw terminal or supply external +5 V at screw terminal Set ENA and/or ENB to +5 V to enable motor permanently or supply ENA and/or ENB with PWM signal IN1 and IN2 set rotation directory for motor A (OUT1/OUT2) IN2 and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
