# Fritzing sketch NANO Вариант (saved by Fritzing 0.9.5d)
breadboards: 1

parts:
  VCC3 = Battery block 9V
  SP3 = SPEAKER [package=pcb_mount_speaker]
  S4 = Momentary Switch [package=ksa_sealed_tac_switch]
  R3 = Resistor [tolerance=±5% resistance=10k package="1206 [SMD]"]
  L298N3 = L298N DC motor driver
  M3 = DC Motor
  Компонент4 = Arduino Nano (Rev3.0)
  DFRobot_DFPlayer_Mini3 = DFRobot DFPlayer Mini [part_number=DFR0299]

nets:
  GND: VCC3.-, R3.Pin_0, L298N3.GND, Компонент4.GND, DFRobot_DFPlayer_Mini3.GND-1, DFRobot_DFPlayer_Mini3.GND-2
  N1: VCC3.+, L298N3.12V
  N2: SP3.+, DFRobot_DFPlayer_Mini3.SPK_2
  N3: SP3.-, DFRobot_DFPlayer_Mini3.SPK_1
  5V: S4.2, Компонент4.5V, DFRobot_DFPlayer_Mini3.VCC
  N4: S4.3, Компонент4.A2
  N5: S4.4, R3.Pin_1
  N6: L298N3.OUT3, M3.pin_2
  N7: L298N3.OUT4, M3.pin_1
  N8: L298N3.5V, L298N3.ENB
  N9: L298N3.IN4, Компонент4.A1
  N10: Компонент4.D4, DFRobot_DFPlayer_Mini3.TX
  N11: Компонент4.D5, DFRobot_DFPlayer_Mini3.RX

custom parts:
  L298N DC motor driver: 2x DC motor driver with 78M05 positive voltage regulator (7..35 V) L298N: max 46 V, 2 A Set 5 V Enable jumper to enable 5 V regultor (needed for the L298N) and +5 V output at screw terminal or supply external +5 V at screw terminal Set ENA and/or ENB to +5 V to enable motor permanently or supply ENA and/or ENB with PWM signal IN1 and IN2 set rotation directory for motor A (OUT1/OUT2) IN2 and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
